// Logisim project calc.circ as structural Verilog: 2 circuits, main circuit main
module main (
  input  A1,
  input  B1,
  input  SIGN_B,
  input  B0,
  input  SIGN_A,
  input  A0,
  input  _01,
  input  _02,
  output C3,
  output C2,
  output C1,
  output C0
);

  wire bcd_to_sigment_1_p5, bcd_to_sigment_1_p6, bcd_to_sigment_1_p7, bcd_to_sigment_1_p8,
       bcd_to_sigment_1_p9, bcd_to_sigment_1_p10, bcd_to_sigment_1_p11, bcd_to_sigment_2_p4,
       bcd_to_sigment_2_p5, bcd_to_sigment_2_p6, bcd_to_sigment_2_p7, bcd_to_sigment_2_p8,
       bcd_to_sigment_2_p9, bcd_to_sigment_2_p10, bcd_to_sigment_4_p5, bcd_to_sigment_4_p6,
       bcd_to_sigment_4_p7, bcd_to_sigment_4_p8, bcd_to_sigment_4_p9, bcd_to_sigment_4_p10,
       bcd_to_sigment_4_p11, bcd_to_sigment_4_p12, calculator_1_divide_by_zero, calculator_1_out_10,
       calculator_1_out_11;

  // BCD_TO_SIGMENT bcd_to_sigment_1: pin names not known; wires that end beside it: 1'b0, 1'b0, B1, B0, bcd_to_sigment_1_p5, bcd_to_sigment_1_p6, bcd_to_sigment_1_p7, bcd_to_sigment_1_p8, bcd_to_sigment_1_p9, bcd_to_sigment_1_p10, bcd_to_sigment_1_p11
  LED divide_by_zero (.in(calculator_1_divide_by_zero));
  LED zero_flag (.in(calculator_1_out_11));
  LED sign_flag (.in(calculator_1_out_10));
  _7_Segment_Display u_7_segment_display_1 (
    .g(bcd_to_sigment_1_p11), .f(bcd_to_sigment_1_p10), .a(bcd_to_sigment_1_p5), .b(bcd_to_sigment_1_p6),
    .e(bcd_to_sigment_1_p9), .d(bcd_to_sigment_1_p8), .c(bcd_to_sigment_1_p7));  // open: dp
  calculator calculator_1 (
    .sign_B(SIGN_B), .B1(B1), .B0(B0), .sign_A(SIGN_A), .A1(A1), .A0(A0), .in_3(_01), .in_4(_02),
    .divide_by_zero(calculator_1_divide_by_zero), .out_13(C1), .out_12(C0), .out_15(C2), .out_14(C3),
    .out_10(calculator_1_out_10), .out_11(calculator_1_out_11));
  // BCD_TO_SIGMENT bcd_to_sigment_2: pin names not known; wires that end beside it: 1'b0, A1, A0, bcd_to_sigment_2_p4, bcd_to_sigment_2_p5, bcd_to_sigment_2_p6, bcd_to_sigment_2_p7, bcd_to_sigment_2_p8, bcd_to_sigment_2_p9, bcd_to_sigment_2_p10
  _7_Segment_Display u_7_segment_display_2 (
    .g(bcd_to_sigment_2_p10), .f(bcd_to_sigment_2_p9), .a(bcd_to_sigment_2_p4), .b(bcd_to_sigment_2_p5),
    .e(bcd_to_sigment_2_p8), .d(bcd_to_sigment_2_p7), .c(bcd_to_sigment_2_p6));  // open: dp
  // BCD_TO_SIGMENT bcd_to_sigment_3: pin names not known; wires that end beside it: calculator_1_out_10, 1'b0, 1'b0, 1'b0
  // BCD_TO_SIGMENT bcd_to_sigment_4: pin names not known; wires that end beside it: C3, C2, C1, C0, bcd_to_sigment_4_p5, bcd_to_sigment_4_p6, bcd_to_sigment_4_p7, bcd_to_sigment_4_p8, bcd_to_sigment_4_p9, bcd_to_sigment_4_p10, bcd_to_sigment_4_p11, bcd_to_sigment_4_p12
  _7_Segment_Display u_7_segment_display_3 (
    .g(bcd_to_sigment_4_p12), .f(bcd_to_sigment_4_p11), .a(bcd_to_sigment_4_p6), .b(bcd_to_sigment_4_p7),
    .e(bcd_to_sigment_4_p10), .d(bcd_to_sigment_4_p9), .c(bcd_to_sigment_4_p8));  // open: dp
  _7_Segment_Display u_7_segment_display_4 (.g(bcd_to_sigment_4_p5));  // open: f, a, b, e, d, c, dp

  // Notes on the sheet:
  //   ADDITION 00
  //   SUBTRACTION 01
  //   MULTIPLICATION 10
  //   DIVISION 11
  //   C=A+B
  //   C=A-B
  //   C=A*B
  //   C=A/B
endmodule

// integration
module calculator (
  input  sign_B,
  input  sign_A,
  input  in_3,
  input  in_4,
  input  B1,
  input  B0,
  input  A1,
  input  A0,
  output divide_by_zero,
  output out_10,
  output out_11,
  output out_12,
  output out_13,
  output out_14,
  output out_15
);

  wire and_1_out, main_2_p9, or_1_out, or_2_out;
  wire [4:0] main_1_p11, main_2_p8, mutliplier_1_p8;

  // Add___Subt_main main_1: pin names not known; wires that end beside it: sign_A, sign_B, in_4, A0, A1, B0, B1, main_1_p11[4], main_1_p11[2], main_1_p11[1], main_1_p11[0]
  LED led_1 (.in(out_10));
  // mutliplier mutliplier_1: pin names not known; wires that end beside it: sign_A, A1, A0, sign_B, B1, B0, mutliplier_1_p8[4], mutliplier_1_p8[0], mutliplier_1_p8[1], mutliplier_1_p8[2], mutliplier_1_p8[3]
  // divide_main main_2: pin names not known; wires that end beside it: A0, A1, B0, B1, sign_A, sign_B, main_2_p8[1], main_2_p8[0], main_2_p9, main_2_p8[4]
  or or_1 (or_1_out, out_15, out_14);
  or or_2 (or_2_out, out_13, or_1_out);
  and and_1 (and_1_out, in_4, in_3);
  and and_2 (divide_by_zero, and_1_out, main_2_p9);
  LED divide_by_zero_flag (.in(divide_by_zero));
  nor nor_1 (out_11, out_12, or_2_out);
  Multiplexer #(.select(2), .width(5), .enable("false")) multiplexer_1 (
    .in0({main_1_p11[4], 1'b0, main_1_p11[2:0]}), .in1({main_1_p11[4], 1'b0, main_1_p11[2:0]}),
    .in2(mutliplier_1_p8), .in3({main_2_p8[4], 2'b00, main_2_p8[1:0]}),
    .out({out_10, out_14, out_15, out_13, out_12}), .sel({in_3, in_4}));

  // Notes on the sheet:
  //   addition 00
  //   subtraction 01
  //   multiplication 10
  //   division 11
endmodule
